# Fritzing sketch Raspberry (saved by Fritzing 0.9.3b)
circuit board: 6.23534cm x 3.00333cm

parts:
  Raspberry_Pi_3 = Raspberry Pi 3 [part_number=RPI-3-V1.2]
  Temp_sensor = IC, DIP package, 8 pins [chip_label=TMP75]
  Body_Sensor = HC-SR501 Body Sensor Module
  LED3 = LED - 5mm [color="Green (555nm)" package="5 mm [THT]"]
  Speaker = Piezo Speaker
  J4 = female pin header, 3 pins [form="♀ (female)"]
  J7 = male pin header, 3 pins [form="♂ (male)"]
  R1 = Resistor [tolerance=±5% resistance=47 package=THT]
  R2 = Resistor [tolerance=±5% resistance=5k package=THT]
  R3 = Resistor [tolerance=±5% resistance=5k package=THT]

nets:
  3V3: Raspberry_Pi_3.3v3, Raspberry_Pi_3.3V3, Temp_sensor.pin5, Temp_sensor.pin6, Temp_sensor.pin7, Temp_sensor.pin8, R2.Pin_0, R3.Pin_0
  N1: Raspberry_Pi_3.GPIO2, Temp_sensor.pin1, R3.Pin_1
  N2: Raspberry_Pi_3.GPIO3, Temp_sensor.pin2, R2.Pin_1
  N3: Raspberry_Pi_3.GND, Temp_sensor.pin4, Speaker.pin1, J7.pin1, R1.Pin_1
  N4: Raspberry_Pi_3.GPIO24, Speaker.pin2
  N5: Raspberry_Pi_3.GPIO23, LED3.anode
  N6: Raspberry_Pi_3.GPIO18, J7.pin2
  N7: Raspberry_Pi_3.5V, J7.pin3
  N8: Body_Sensor.VCC, J4.pin3
  N9: Body_Sensor.OUT, J4.pin2
  N10: Body_Sensor.GND, J4.pin1
  N11: LED3.cathode, R1.Pin_0

custom parts:
  HC-SR501 Body Sensor Module: Pyroelectric Infrared PIR Motion Sensor Detector Module
